# Fritzing sketch 20150604-Basetta (saved by Fritzing 0.9.2b)
perfboards: 1

parts:
  D1 = Rectifier Diode [part_number=1N4007 package="300 mil [THT]"]
  D2 = Rectifier Diode [part_number=1N4007 package="300 mil [THT]"]
  D3 = Rectifier Diode [part_number=1N4007 package="300 mil [THT]"]
  D4 = Rectifier Diode [part_number=1N4007 package="300 mil [THT]"]
  R1 = Resistor [tolerance=±5% resistance=330 package=THT]
  R2 = Resistor [tolerance=±5% resistance=330 package=THT]
  R3 = Resistor [tolerance=±5% resistance=330 package=THT]
  R4 = Resistor [tolerance=±5% resistance=330 power=1W package=THT]
  J1 = female pin header, 2 pins [form="♀ (female)"]
  J2 = female pin header, 2 pins [form="♀ (female)"]
  J3 = female pin header, 2 pins [form="♀ (female)"]
  J4 = female pin header, 2 pins [form="♀ (female)"]
  Power_plug1 = Power plug
  J5 = female pin header, 2 pins [form="♀ (female)"]
  J6 = female pin header, 2 pins [form="♀ (female)"]
  J7 = female pin header, 2 pins [form="♀ (female)"]
  J8 = female pin header, 2 pins [form="♀ (female)"]
  R5 = Trimmer Potentiometer [maximum_resistance=10kΩ package=THT]
  J9 = female pin header, 2 pins [form="♀ (female)"]
  J10 = female pin header, 2 pins [form="♀ (female)"]
  R6 = Trimmer Potentiometer [maximum_resistance=10kΩ package=THT]
  R7 = Trimmer Potentiometer [maximum_resistance=10kΩ package=THT]
  R8 = Trimmer Potentiometer [maximum_resistance=10kΩ package=THT]
  J11 = female pin header, 2 pins [form="♀ (female)"]
  J12 = female pin header, 2 pins [form="♀ (female)"]
  J13 = female pin header, 2 pins [form="♀ (female)"]
  J14 = female pin header, 2 pins [form="♀ (female)"]
  J15 = female pin header, 2 pins [form="♀ (female)"]
  J16 = female pin header, 2 pins [form="♀ (female)"]
  J17 = female pin header, 2 pins [form="♀ (female)"]
  J18 = female pin header, 2 pins [form="♀ (female)"]
  J19 = female pin header, 2 pins [form="♀ (female)"]
  J20 = female pin header, 2 pins [form="♀ (female)"]
  J21 = female pin header, 2 pins [form="♀ (female)"]

nets:
  N1: D1.cathode, D2.cathode, D3.cathode, D4.cathode, Power_plug1.GND, J5.pin2, J6.pin2, J7.pin2, J8.pin2
  N2: D1.anode, R1.Pin_0
  N3: D2.anode, R2.Pin_0
  N4: D3.anode, R3.Pin_0
  N5: D4.anode, R4.Pin_0
  N6: R1.Pin_1, J1.pin1, J5.pin1
  N7: R2.Pin_1, J2.pin1, J6.pin1
  N8: R3.Pin_1, J3.pin1, J7.pin1
  N9: R4.Pin_1, J4.pin1, J8.pin1
  N10: J1.pin2, J2.pin2, J3.pin2, J4.pin2, Power_plug1.VCC
  N11: R5.leg1, J10.pin1
  N12: R5.wiper, J14.pin2
  N13: R5.leg2, J9.pin2, J10.pin2, R6.leg2, R7.leg2, R8.leg2, J11.pin2, J12.pin2, J13.pin2, J16.pin1, J18.pin2, J20.pin1, J21.pin2
  N14: J9.pin1, J16.pin2, J17.pin1, J19.pin1, J20.pin2
  N15: R6.leg1, J11.pin1
  N16: R6.wiper, J14.pin1
  N17: R7.leg1, J12.pin1
  N18: R7.wiper, J15.pin2
  N19: R8.leg1, J13.pin1
  N20: R8.wiper, J15.pin1

notes:
  +
  -
  330
  30/70
  to relays
  from/to PIR
  to solenoids
  from turntables
